// Logisim project aialu.circ as structural Verilog: 16 circuits, main circuit AIALU 2.0
module AiArith_1_0 (
  input  [7:0] A,
  input  in_2,
  input  [7:0] B,
  input  in_4,
  output [7:0] out_5,
  output out_6
);

  aiArith aiarith_1 (.A(A), .in_2(in_4), .B(B), .out_5(out_5), .in_4(in_2), .out_6(out_6));
endmodule

// a
module aiArith (
  input  [7:0] A,
  input  in_2,
  input  [7:0] B,
  input  in_4,
  output [7:0] out_5,
  output out_6
);

  wire a_t, and_1_out, and_2_out, b_t, not_1_out;
  wire [7:0] sommatore_8_bits_1_out_4, sottr_8_bits_1_p5;

  // sottr__8_bits sottr_8_bits_1: pin names not known; wires that end beside it: A, B, in_2, a_t, sottr_8_bits_1_p5
  sommatore_8_bits sommatore_8_bits_1 (.A(A), .B(B), .C(b_t), .out_4(sommatore_8_bits_1_out_4));
  not not_1 (not_1_out, in_2);
  and and_1 (and_1_out, not_1_out, a_t);
  and and_2 (and_2_out, in_2, b_t);
  sommatore_8_bits sommatore_8_bits_2 (.A(sottr_8_bits_1_p5), .B(sommatore_8_bits_1_out_4), .out_4(out_5));  // open: C
  or or_1 (out_6, and_1_out, and_2_out);

  // Other names for the same wires on the sheet: e = in_2
endmodule

module sottr__8_bits (
  input  [7:0] A,
  input  [7:0] B,
  output out_3,
  output [7:0] out_4
);

  wire _1, _2, _3, _4, _5, _6, _7, _8, _77, and_7_out, f_a_1_c_2, f_a_1_s, f_a_2_c_2, f_a_2_s, f_a_3_c_2,
       f_a_3_s, f_a_4_c_2, f_a_4_s, f_a_5_c_2, f_a_5_s, f_a_6_c_2, f_a_6_s, f_a_7_c_2, f_a_7_s, f_a_8_c_2,
       f_a_8_s, not_1_out;

  f_a f_a_1 (.a(_8), .b(A[0]), .c(1'b1), .s(f_a_1_s), .c_2(f_a_1_c_2));
  not not_1 (not_1_out, 1'b0);
  assign {_1, _2, _3, _4, _5, _6, _7, _8} = ~B;  // NOT_Gate not_2, 8 bits wide
  f_a f_a_2 (.a(_7), .b(A[1]), .c(f_a_1_c_2), .s(f_a_2_s), .c_2(f_a_2_c_2));
  and and_1 (out_4[0], f_a_1_s, not_1_out);
  f_a f_a_3 (.a(_6), .b(A[2]), .c(f_a_2_c_2), .s(f_a_3_s), .c_2(f_a_3_c_2));
  and and_2 (out_4[1], f_a_2_s, not_1_out);
  f_a f_a_4 (.a(_5), .b(A[3]), .c(f_a_3_c_2), .s(f_a_4_s), .c_2(f_a_4_c_2));
  and and_3 (out_4[2], f_a_3_s, not_1_out);
  f_a f_a_5 (.a(_4), .b(A[4]), .c(f_a_4_c_2), .s(f_a_5_s), .c_2(f_a_5_c_2));
  and and_4 (out_4[3], f_a_4_s, not_1_out);
  and and_5 (out_4[4], f_a_5_s, not_1_out);
  f_a f_a_6 (.a(_3), .b(A[5]), .c(f_a_5_c_2), .s(f_a_6_s), .c_2(f_a_6_c_2));
  and and_6 (out_4[5], f_a_6_s, not_1_out);
  xnor xnor_1 (_77, A[7], _1);
  and and_7 (and_7_out, A[7], _1, _77);
  f_a f_a_7 (.a(_2), .b(A[6]), .c(f_a_6_c_2), .s(f_a_7_s), .c_2(f_a_7_c_2));
  and and_8 (out_4[6], f_a_7_s, not_1_out);
  f_a f_a_8 (.a(_1), .b(A[7]), .c(f_a_7_c_2), .s(f_a_8_s), .c_2(f_a_8_c_2));
  and and_9 (out_4[7], f_a_8_s, not_1_out);
  and and_10 (out_3, and_7_out, f_a_8_c_2);

  // Other names for the same wires on the sheet: h = A[0]; g = A[1]; f = A[2]; e = A[3]; d = A[4]; c = A[5];
  //   b_t = A[6]; a_t = A[7]
endmodule

module sommatore_8_bits (
  input  [7:0] A,
  input  [7:0] B,
  output C,
  output [7:0] out_4
);

  wire half_adder_1_out_3, half_adder_1_out_4, half_adder_1_out_5, half_adder_1_out_6, half_adder_1_out_7,
       half_adder_1_out_8, half_adder_1_out_9, half_adder_1_out_10;

  half_adder half_adder_1 (
    .A(A), .B(B), .out_3(half_adder_1_out_3), .out_4(half_adder_1_out_4), .out_5(half_adder_1_out_5),
    .out_6(half_adder_1_out_6), .out_7(half_adder_1_out_7), .out_8(half_adder_1_out_8),
    .out_9(half_adder_1_out_9), .out_10(half_adder_1_out_10), .out_11(C));
  and and_1 (out_4[7], half_adder_1_out_3, 1'b1);
  and and_2 (out_4[6], half_adder_1_out_4, 1'b1);
  and and_3 (out_4[5], half_adder_1_out_5, 1'b1);
  and and_4 (out_4[4], half_adder_1_out_6, 1'b1);
  and and_5 (out_4[3], half_adder_1_out_7, 1'b1);
  and and_6 (out_4[2], half_adder_1_out_8, 1'b1);
  and and_7 (out_4[1], half_adder_1_out_9, 1'b1);
  and and_8 (out_4[0], half_adder_1_out_10, 1'b1);
endmodule

module half_adder (
  input  [7:0] A,
  input  [7:0] B,
  output out_3,
  output out_4,
  output out_5,
  output out_6,
  output out_7,
  output out_8,
  output out_9,
  output out_10,
  output out_11
);

  wire f_a_2_c_2, f_a_3_c_2, f_a_4_c_2, f_a_5_c_2, f_a_6_c_2, f_a_7_c_2, f_a_8_c_2;

  f_a f_a_1 (.a(A[7]), .b(B[7]), .c(f_a_2_c_2), .s(out_3), .c_2(out_11));
  f_a f_a_2 (.a(A[6]), .b(B[6]), .c(f_a_3_c_2), .s(out_4), .c_2(f_a_2_c_2));
  f_a f_a_3 (.a(A[5]), .b(B[5]), .c(f_a_4_c_2), .s(out_5), .c_2(f_a_3_c_2));
  f_a f_a_4 (.a(A[4]), .b(B[4]), .c(f_a_5_c_2), .s(out_6), .c_2(f_a_4_c_2));
  f_a f_a_5 (.a(A[3]), .b(B[3]), .c(f_a_6_c_2), .s(out_7), .c_2(f_a_5_c_2));
  f_a f_a_6 (.a(A[2]), .b(B[2]), .c(f_a_7_c_2), .s(out_8), .c_2(f_a_6_c_2));
  f_a f_a_7 (.a(A[1]), .b(B[1]), .c(f_a_8_c_2), .s(out_9), .c_2(f_a_7_c_2));
  f_a f_a_8 (.a(A[0]), .b(B[0]), .c(1'b0), .s(out_10), .c_2(f_a_8_c_2));
endmodule

module h_a (
  input  a,
  input  b,
  output s,
  output c
);

  wire and_2_out, and_3_out, not_1_out, not_2_out;

  not not_1 (not_1_out, a);
  not not_2 (not_2_out, b);
  and and_1 (c, a, b);
  and and_2 (and_2_out, not_1_out, b);
  and and_3 (and_3_out, a, not_2_out);
  or or_1 (s, and_2_out, and_3_out);
endmodule

module f_a (
  input  a,
  input  b,
  input  c,
  output s,
  output c_2
);

  wire and_1_out, and_2_out, and_3_out, and_4_out, and_5_out, and_6_out, and_7_out, not_1_out, not_2_out,
       not_3_out, not_4_out, not_5_out, not_6_out;

  not not_1 (not_1_out, a);
  not not_2 (not_2_out, b);
  not not_3 (not_3_out, a);
  not not_4 (not_4_out, c);
  not not_5 (not_5_out, b);
  not not_6 (not_6_out, c);
  and and_1 (and_1_out, b, c);
  and and_2 (and_2_out, a, c);
  and and_3 (and_3_out, a, b);
  and and_4 (and_4_out, not_1_out, not_2_out, c);
  and and_5 (and_5_out, not_3_out, b, not_4_out);
  and and_6 (and_6_out, a, not_5_out, not_6_out);
  and and_7 (and_7_out, a, b, c);
  or or_1 (c_2, and_1_out, and_2_out, and_3_out);
  or or_2 (s, and_4_out, and_5_out, and_6_out, and_7_out);
endmodule

module AND_A (
  input  [7:0] in_1,
  input  [7:0] in_2,
  output [7:0] out_3
);

  assign out_3 = in_1 & in_2;  // AND_Gate and_1, 8 bits wide
endmodule

module NOT_A (
  input  [7:0] in_1,
  output [7:0] out_2
);

  assign out_2 = ~in_1;  // NOT_Gate not_1, 8 bits wide
endmodule

module OR_A (
  input  [7:0] in_1,
  input  [7:0] in_2,
  output [7:0] out_3
);

  assign out_3 = in_1 | in_2;  // OR_Gate or_1, 8 bits wide
endmodule

module XOR_A (
  input  [7:0] in_1,
  input  [7:0] in_2,
  output [7:0] out_3
);

  assign out_3 = in_1 ^ in_2;  // XOR_Gate xor_1, 8 bits wide
endmodule

module NOT_B (
  input  [7:0] in_1,
  output [7:0] out_2
);

  assign out_2 = ~in_1;  // NOT_Gate not_1, 8 bits wide
endmodule

module MUX_8_bits (
  input  in_1,
  input  in_2,
  input  in_3,
  input  in_4,
  input  in_5,
  input  in_6,
  input  in_7,
  input  in_8,
  input  in_9,
  input  in_10,
  input  in_11,
  output out_12
);

  wire and_1_out, and_2_out, and_3_out, and_4_out, and_5_out, and_6_out, and_7_out, and_8_out, not_1_out,
       not_2_out, not_3_out;

  not not_1 (not_1_out, in_1);
  not not_2 (not_2_out, in_2);
  not not_3 (not_3_out, in_3);
  and and_1 (and_1_out, not_1_out, not_2_out, in_4, not_3_out);
  and and_2 (and_2_out, not_1_out, not_2_out, in_3, in_5);
  and and_3 (and_3_out, not_1_out, in_3, in_6, not_3_out);
  and and_4 (and_4_out, not_1_out, in_2, in_3, in_7);
  and and_5 (and_5_out, in_1, not_2_out, not_3_out, in_8);
  and and_6 (and_6_out, in_1, not_2_out, in_3, in_9);
  and and_7 (and_7_out, in_1, in_3, in_10, not_3_out);
  and and_8 (and_8_out, in_3, in_2, in_11, in_1);
  or or_1 (out_12, and_1_out, and_2_out, and_3_out, and_4_out, and_5_out, and_6_out, and_7_out, and_8_out);
endmodule

// D1
module muxx (
  input  in_1,
  input  in_2,
  input  in_3,
  input  [7:0] A,
  input  [7:0] B,
  input  [7:0] C,
  input  [7:0] D,
  input  [7:0] E,
  input  [7:0] F,
  input  [7:0] G,
  input  [7:0] H,
  output [7:0] out_12
);

  MUX_8_bits mux_8_bits_1 (
    .in_4(A[0]), .in_5(B[0]), .in_6(C[0]), .in_7(D[0]), .in_8(E[0]), .in_9(F[0]), .in_10(G[0]), .in_11(H[0]),
    .in_1(in_1), .in_2(in_2), .in_3(in_3), .out_12(out_12[0]));
  MUX_8_bits mux_8_bits_2 (
    .in_4(A[1]), .in_5(B[1]), .in_6(C[1]), .in_7(D[1]), .in_8(E[1]), .in_9(F[1]), .in_10(G[1]), .in_11(H[1]),
    .in_1(in_1), .in_2(in_2), .in_3(in_3), .out_12(out_12[1]));
  MUX_8_bits mux_8_bits_3 (
    .in_4(A[2]), .in_5(B[2]), .in_6(C[2]), .in_7(D[2]), .in_8(E[2]), .in_9(F[2]), .in_10(G[2]), .in_11(H[2]),
    .in_1(in_1), .in_2(in_2), .in_3(in_3), .out_12(out_12[2]));
  MUX_8_bits mux_8_bits_4 (
    .in_4(A[3]), .in_5(B[3]), .in_6(C[3]), .in_7(D[3]), .in_8(E[3]), .in_9(F[3]), .in_10(G[3]), .in_11(H[3]),
    .in_1(in_1), .in_2(in_2), .in_3(in_3), .out_12(out_12[3]));
  MUX_8_bits mux_8_bits_5 (
    .in_4(A[4]), .in_5(B[4]), .in_6(C[4]), .in_7(D[4]), .in_8(E[4]), .in_9(F[4]), .in_10(G[4]), .in_11(H[4]),
    .in_1(in_1), .in_2(in_2), .in_3(in_3), .out_12(out_12[4]));
  MUX_8_bits mux_8_bits_6 (
    .in_4(A[5]), .in_5(B[5]), .in_6(C[5]), .in_7(D[5]), .in_8(E[5]), .in_9(F[5]), .in_10(G[5]), .in_11(H[5]),
    .in_1(in_1), .in_2(in_2), .in_3(in_3), .out_12(out_12[5]));
  MUX_8_bits mux_8_bits_7 (
    .in_4(A[6]), .in_5(B[6]), .in_6(C[6]), .in_7(D[6]), .in_8(E[6]), .in_9(F[6]), .in_10(G[6]), .in_11(H[6]),
    .in_1(in_1), .in_2(in_2), .in_3(in_3), .out_12(out_12[6]));
  MUX_8_bits mux_8_bits_8 (
    .in_4(A[7]), .in_5(B[7]), .in_6(C[7]), .in_7(D[7]), .in_8(E[7]), .in_9(F[7]), .in_10(G[7]), .in_11(H[7]),
    .in_1(in_1), .in_2(in_2), .in_3(in_3), .out_12(out_12[7]));

  // Other names for the same wires on the sheet: A_t = out_12[0]; B_t = out_12[1]; C_t = out_12[2]; D_t = out_12[3];
  //   E_t = out_12[4]; F_t = out_12[5]; G_t = out_12[6]; H_t = out_12[7]; x = in_1; y = in_2; z = in_3
endmodule

module AIALU (
  input  [7:0] A,
  input  [7:0] B,
  input  [2:0] in_3,
  input  in_4,
  output out_5,
  output [7:0] out_6,
  output out_7
);

  wire [7:0] and_a_1_out_3, muxx_1_out_12, not_a_1_out_2, not_b_1_out_2, or_a_1_out_3,
       sommatore_8_bits_1_out_4, sottr_8_bits_1_out_4, xor_a_1_out_3;

  sommatore_8_bits sommatore_8_bits_1 (.A(A), .B(B), .C(out_7), .out_4(sommatore_8_bits_1_out_4));
  sottr__8_bits sottr_8_bits_1 (.A(A), .B(B), .out_4(sottr_8_bits_1_out_4), .out_3(out_5));
  AND_A and_a_1 (.in_1(A), .in_2(B), .out_3(and_a_1_out_3));
  OR_A or_a_1 (.in_1(A), .in_2(B), .out_3(or_a_1_out_3));
  XOR_A xor_a_1 (.in_1(A), .in_2(B), .out_3(xor_a_1_out_3));
  NOT_A not_a_1 (.in_1(A), .out_2(not_a_1_out_2));
  NOT_B not_b_1 (.in_1(B), .out_2(not_b_1_out_2));
  muxx muxx_1 (
    .in_1(in_3[2]), .in_2(in_3[1]), .in_3(in_3[0]), .A(sommatore_8_bits_1_out_4), .B(sottr_8_bits_1_out_4),
    .C(and_a_1_out_3), .D(or_a_1_out_3), .E(xor_a_1_out_3), .F(not_a_1_out_2), .G(not_b_1_out_2),
    .H({8{1'b0}}), .out_12(muxx_1_out_12));
  sommatore_8_bits sommatore_8_bits_2 (.A(muxx_1_out_12), .B({{7{1'b0}}, in_4}), .out_4(out_6));  // open: C
endmodule

module AIALU_2_0 (
  input  [7:0] A,
  input  [2:0] SELETTORE,
  input  [7:0] B,
  input  CARRY_IN,
  output [7:0] out_5
);

  wire aialu_1_out_5, aialu_1_out_7;

  // Probe on A
  // Probe on B
  AIALU aialu_1 (
    .out_7(aialu_1_out_7), .A(A), .B(B), .out_5(aialu_1_out_5), .in_4(CARRY_IN), .out_6(out_5),
    .in_3(SELETTORE));
  // Probe on out_5
  LED OVERFLOW (.in(aialu_1_out_7));
  LED CARRY (.in(aialu_1_out_5));

  // Notes on the sheet:
  //   RISULTATO
endmodule
